// Logisim project ISA.circ as structural Verilog
module my_circuit (
  input  in_1,
  input  in_2,
  input  in_3,
  input  in_4,
  input  in_5,
  input  in_6,
  output out_7
);

  wire [31:0] adder_1_out, PC_q;

  Adder #(.width(32)) adder_1 (.a(PC_q), .b(32'h4), .out(adder_1_out));  // open: cin, cout
  Register #(.width(32)) PC (.D(adder_1_out), .en(in_2), .Q(PC_q), .clk(in_3), .clr(in_4));
  memory MEMORY (.MAR_IN(PC_q), .in_5(in_3), .LD_MAR(in_5), .LD_MDR(in_6));  // open: in_4, out_6

  assign out_7 = in_1;

  // Other names for the same wires on the sheet: CK = in_3; CLR_PC = in_4; LD_MAR = in_5; LD_MDR = in_6; LD_PC = in_2
endmodule

module memory (
  input  [31:0] MAR_IN,
  input  LD_MAR,
  input  LD_MDR,
  input  in_4,
  input  in_5,
  output [31:0] out_6
);

  wire [1:0] BYTE;
  wire [5:0] CRAP;
  wire [7:0] multiplexer_1_out, ram_1_data, ram_2_data, ram_3_data, ram_4_data;
  wire [25:2] MAR_q;
  wire [31:0] bit_extender_1_out, multiplexer_2_out;

  Register #(.width(32)) MAR (.D(MAR_IN), .en(LD_MAR), .Q({CRAP, MAR_q, BYTE}), .clk(in_4));  // open: clr
  RAM #(.addrWidth(24)) ram_1 (.addr(MAR_q), .data(ram_1_data), .clk(in_4), .ld(1'b1));  // open: sel, clr
  RAM #(.addrWidth(24)) ram_2 (.addr(MAR_q), .data(ram_2_data), .clk(in_4), .ld(1'b1));  // open: sel, clr
  RAM #(.addrWidth(24)) ram_3 (.addr(MAR_q), .data(ram_3_data), .clk(in_4), .ld(1'b1));  // open: sel, clr
  RAM #(.addrWidth(24)) ram_4 (.addr(MAR_q), .data(ram_4_data), .clk(in_4), .ld(1'b1));  // open: sel, clr
  Multiplexer #(.select(2), .width(8), .disabled(0), .enable("false")) multiplexer_1 (
    .in0(ram_1_data), .in1(ram_2_data), .in2(ram_3_data), .in3(ram_4_data), .out(multiplexer_1_out),
    .sel(BYTE));
  assign bit_extender_1_out = {{24{1'b0}}, multiplexer_1_out};  // Bit_Extender bit_extender_1
  Multiplexer #(.width(32), .disabled(0), .enable("false")) multiplexer_2 (
    .in0({ram_4_data, ram_3_data, ram_2_data, ram_1_data}), .in1(bit_extender_1_out),
    .out(multiplexer_2_out), .sel(in_5));
  Register #(.width(32)) MDR (.D(multiplexer_2_out), .en(LD_MDR), .Q(out_6), .clk(in_4));  // open: clr

  // Other names for the same wires on the sheet: CK = in_4; SIZE = in_5
endmodule

module register_file (
  input  [31:0] DATA_IN,
  input  [3:0] DST_REG,
  input  [3:0] REG_A,
  input  [3:0] REG_B,
  input  WE,
  output [31:0] OUT_A,
  output [31:0] OUT_B
);

  Register #(.width(32)) register_1 ();  // open: D, en, Q, clk, clr
  Register #(.width(32)) register_2 ();  // open: D, en, Q, clk, clr
  Register #(.width(32)) register_3 ();  // open: D, en, Q, clk, clr
  Register #(.width(32)) register_4 ();  // open: D, en, Q, clk, clr
  Register #(.width(32)) register_5 ();  // open: D, en, Q, clk, clr
  Register #(.width(32)) register_6 ();  // open: D, en, Q, clk, clr
  Register #(.width(32)) register_7 ();  // open: D, en, Q, clk, clr
  Register #(.width(32)) register_8 ();  // open: D, en, Q, clk, clr
  Register #(.width(32)) register_9 ();  // open: D, en, Q, clk, clr
  Register #(.width(32)) register_10 ();  // open: D, en, Q, clk, clr
  Register #(.width(32)) register_11 ();  // open: D, en, Q, clk, clr
  Register #(.width(32)) register_12 ();  // open: D, en, Q, clk, clr
  Register #(.width(32)) register_13 ();  // open: D, en, Q, clk, clr
  Register #(.width(32)) register_14 ();  // open: D, en, Q, clk, clr
  Register #(.width(32)) register_15 ();  // open: D, en, Q, clk, clr
  Register #(.width(32)) register_16 ();  // open: D, en, Q, clk, clr
  Demultiplexer #(.select(2), .width(32), .disabled(0), .enable("false")) demultiplexer_1 (.in(OUT_A));  // open: out0, out1, out2, out3, sel
  Demultiplexer #(.select(2), .width(32), .disabled(0), .enable("false")) demultiplexer_2 (.in(OUT_B));  // open: out0, out1, out2, out3, sel
endmodule
