// Logisim project PipelinedLC2200.circ as structural Verilog
module FBUF (
  input  [31:0] INPUT,
  input  LOAD,
  input  CLOCK,
  output [7:0] OPCODE,
  output [3:0] REG_DST,
  output [3:0] REG_SR1,
  output [3:0] REG_SR2,
  output [15:0] IMMEDIATE
);

  Register #(.width(32)) FBUF (
    .D(INPUT), .en(LOAD), .Q({OPCODE, REG_DST, REG_SR1, IMMEDIATE[3:0], IMMEDIATE[15:4]}), .clk(CLOCK));  // open: clr

  assign REG_SR2 = IMMEDIATE[3:0];
endmodule
